# Fritzing sketch Project11 Fritzing (saved by Fritzing 0.9.0b)
breadboards: 1

parts:
  Part1 = Arduino Uno (Rev3)
  R1 = Resistor [package="0402 [SMD]"]
  S1 = Momentary Switch [package=ksa_sealed_tac_switch]
  R2 = Resistor [tolerance=±5% resistance=10k package="0603 [SMD]"]
  LED2 = RGB LED - (4 legs) [package="5 mm [THT]"]
  PIR1 = PIR sensor
  DHT1 = DHT11 Humitidy and Temperature Sensor
  J1 = Piezo Speaker
  R3 = Photocell (LDR) [package=THT]
  R4 = Resistor [tolerance=±5% resistance=10k package="0603 [SMD]"]
  LED3 = RGB LED - (4 legs) [package="5 mm [THT]"]
  R7 = Resistor [package="0402 [SMD]"]

nets:
  N1: Part1.A5/SCL, R3.pin_1, R4.Pin_0
  N2: Part1.D8, PIR1.SIG
  N3: Part1.D9_PWM, LED3.blue_cathode
  N4: Part1.D10_PWM/SS, LED3.green_cathode
  N5: Part1.D11_PWM/MOSI, LED3.red_cathode
  N6: Part1.D2, S1.2, R2.Pin_0
  N7: Part1.D3_PWM, LED2.green_cathode
  N8: Part1.D5_PWM, LED2.red_cathode
  N9: Part1.D6_PWM, J1.pin2
  N10: Part1.D7, DHT1.DATA
  VDD: Part1.5V, R1.Pin_1, S1.4, PIR1.VDD, DHT1.VDD, J1.pin1, R3.pin_0, R7.Pin_1
  GND: Part1.GND, R2.Pin_1, PIR1.GND, DHT1.GND, R4.Pin_1
  N11: R1.Pin_0, LED2.common_anode
  N12: LED3.common_anode, R7.Pin_0

custom parts:
  DHT11 Humitidy and Temperature Sensor: DHT11 Humidity and Temperature Sensor
