# Fritzing sketch Project4 Fritzing (saved by Fritzing 0.9.0b)
breadboards: 1

parts:
  Part1 = Arduino Uno (Rev3)
  R1 = Resistor [package="0402 [SMD]"]
  LED1 = smd LED [color="Red (633nm)" package="0805 [SMD]"]
  R2 = PHOTOCELL [package=photocell-kit]
  R3 = Resistor [tolerance=±5% resistance=10k package=THT]

nets:
  N1: Part1.A0, R2.P$2, R3.Pin_0
  N2: Part1.D11_PWM/MOSI, R1.Pin_0
  N3: Part1.5V, R2.P$1
  N4: Part1.GND, LED1.cathode, R3.Pin_1
  N5: R1.Pin_1, LED1.anode
